// Digital circuit add-sub.dig as structural Verilog
module add_sub (
  input  [31:0] B,
  input  [31:0] A,
  input  Sub,
  output [31:0] Out,
  output Overflow,
  output Sign
);

  wire not_2_out, xor_1_out, xor_2_out, xor_3_out;
  wire [31:0] multiplexer_1_out, not_1_out;

  assign not_1_out = ~B;  // Not not_1, 32 bits wide
  xor xor_1 (xor_1_out, Sub, B[31]);
  Multiplexer #(.Bits(32)) multiplexer_1 (.sel(Sub), .in_0(B), .in_1(not_1_out), .out(multiplexer_1_out));
  xor xor_2 (xor_2_out, A[31], xor_1_out);
  Add #(.Bits(32)) add_1 (.a(A), .b(multiplexer_1_out), .c_i(Sub), .s(Out));  // open: c_o
  xor xor_3 (xor_3_out, A[31], Out[31]);
  not not_2 (not_2_out, xor_2_out);
  and and_1 (Overflow, not_2_out, xor_3_out);

  assign Sign = Out[31];
endmodule

/* Test case Add-Sub Test:
A B Sub Out Overflow Sign
0x289322C4 0x01846399 0 0x2A17865D 0 0
0x4152A22D 0x22042121 0 0x6356C34E 0 0
0x84893212 0x0994AD1A 0 0x8E1DDF2C 0 1
0x90A8826C 0x112109FB 0 0xA1C98C67 0 1
0x5210C12D 0x3D04ABBC 0 0x8F156CE9 1 1
0x90D194B5 0xB005500E 0 0x40D6E4C3 1 0
0x39332544 0x0435FCAD 1 0x34FD2897 0 0
0x59286AB1 0x221FB76C 1 0x3708B345 0 0
0xECD55935 0x248C5A4B 1 0xC848FEEA 0 1
0x902A9525 0xE5454D48 1 0xAAE547DD 0 1
0x8211036A 0x7B13890A 1 0x06FD7A60 1 0
0x5FE15DBE 0x8934B9B1 1 0xD6ACA40D 1 1
*/
