// Digital circuit register-file.dig as structural Verilog
module register_file (
  input  [4:0] ReadReg1,
  input  [4:0] ReadReg2,
  input  [4:0] WriteReg,
  input  [31:0] WriteData,
  input  RegWrite,
  input  Clock,
  output [31:0] ReadData1,
  output [31:0] ReadData2
);

  wire and_1_out, and_2_out, and_3_out, and_4_out, and_5_out, and_6_out, and_7_out, and_8_out, and_9_out,
       and_10_out, and_11_out, and_12_out, and_13_out, and_14_out, and_15_out, and_16_out, and_17_out,
       and_18_out, and_19_out, and_20_out, and_21_out, and_22_out, and_23_out, and_24_out, and_25_out,
       and_26_out, and_27_out, and_28_out, and_29_out, and_30_out, and_31_out, WriteReg0, WriteReg1,
       WriteReg2, WriteReg3, WriteReg4, WriteReg5, WriteReg6, WriteReg7, WriteReg8, WriteReg9, WriteReg10,
       WriteReg11, WriteReg12, WriteReg13, WriteReg14, WriteReg15, WriteReg16, WriteReg17, WriteReg18,
       WriteReg19, WriteReg20, WriteReg21, WriteReg22, WriteReg23, WriteReg24, WriteReg25, WriteReg26,
       WriteReg27, WriteReg28, WriteReg29, WriteReg30, WriteReg31;
  wire [31:0] Reg1Output, Reg2Output, Reg3Output, Reg4Output, Reg5Output, Reg6Output, Reg7Output, Reg8Output,
       Reg9Output, Reg10Output, Reg11Output, Reg12Output, Reg13Output, Reg14Output, Reg15Output, Reg16Output,
       Reg17Output, Reg18Output, Reg19Output, Reg20Output, Reg21Output, Reg22Output, Reg23Output,
       Reg24Output, Reg25Output, Reg26Output, Reg27Output, Reg28Output, Reg29Output, Reg30Output, Reg31Output;

  Decoder #(.Selector_Bits(5)) decoder_1 (
    .sel(WriteReg), .out_0(WriteReg0), .out_1(WriteReg1), .out_2(WriteReg2), .out_3(WriteReg3),
    .out_4(WriteReg4), .out_5(WriteReg5), .out_6(WriteReg6), .out_7(WriteReg7), .out_8(WriteReg8),
    .out_9(WriteReg9), .out_10(WriteReg10), .out_11(WriteReg11), .out_12(WriteReg12), .out_13(WriteReg13),
    .out_14(WriteReg14), .out_15(WriteReg15), .out_16(WriteReg16), .out_17(WriteReg17), .out_18(WriteReg18),
    .out_19(WriteReg19), .out_20(WriteReg20), .out_21(WriteReg21), .out_22(WriteReg22), .out_23(WriteReg23),
    .out_24(WriteReg24), .out_25(WriteReg25), .out_26(WriteReg26), .out_27(WriteReg27), .out_28(WriteReg28),
    .out_29(WriteReg29), .out_30(WriteReg30), .out_31(WriteReg31));
  and and_1 (and_1_out, RegWrite, WriteReg1);
  and and_2 (and_2_out, RegWrite, WriteReg2);
  and and_3 (and_3_out, RegWrite, WriteReg3);
  and and_4 (and_4_out, RegWrite, WriteReg4);
  and and_5 (and_5_out, RegWrite, WriteReg5);
  and and_6 (and_6_out, RegWrite, WriteReg6);
  and and_7 (and_7_out, RegWrite, WriteReg7);
  and and_8 (and_8_out, RegWrite, WriteReg8);
  Register #(.Bits(32)) Reg1 (.D(WriteData), .C(Clock), .en(and_1_out), .Q(Reg1Output));
  Register #(.Bits(32)) Reg2 (.D(WriteData), .C(Clock), .en(and_2_out), .Q(Reg2Output));
  Register #(.Bits(32)) Reg3 (.D(WriteData), .C(Clock), .en(and_3_out), .Q(Reg3Output));
  Register #(.Bits(32)) Reg4 (.D(WriteData), .C(Clock), .en(and_4_out), .Q(Reg4Output));
  Register #(.Bits(32)) Reg5 (.D(WriteData), .C(Clock), .en(and_5_out), .Q(Reg5Output));
  Register #(.Bits(32)) Reg6 (.D(WriteData), .C(Clock), .en(and_6_out), .Q(Reg6Output));
  Register #(.Bits(32)) Reg7 (.D(WriteData), .C(Clock), .en(and_7_out), .Q(Reg7Output));
  Register #(.Bits(32)) Reg8 (.D(WriteData), .C(Clock), .en(and_8_out), .Q(Reg8Output));
  Multiplexer #(.Bits(32), .Selector_Bits(5)) multiplexer_1 (
    .sel(ReadReg1), .in_0({32{1'b0}}), .in_1(Reg1Output), .in_2(Reg2Output), .in_3(Reg3Output),
    .in_4(Reg4Output), .in_5(Reg5Output), .in_6(Reg6Output), .in_7(Reg7Output), .in_8(Reg8Output),
    .in_9(Reg9Output), .in_10(Reg10Output), .in_11(Reg11Output), .in_12(Reg12Output), .in_13(Reg13Output),
    .in_14(Reg14Output), .in_15(Reg15Output), .in_16(Reg16Output), .in_17(Reg17Output), .in_18(Reg18Output),
    .in_19(Reg19Output), .in_20(Reg20Output), .in_21(Reg21Output), .in_22(Reg22Output), .in_23(Reg23Output),
    .in_24(Reg24Output), .in_25(Reg25Output), .in_26(Reg26Output), .in_27(Reg27Output), .in_28(Reg28Output),
    .in_29(Reg29Output), .in_30(Reg30Output), .in_31(Reg31Output), .out(ReadData1));
  and and_9 (and_9_out, RegWrite, WriteReg9);
  and and_10 (and_10_out, RegWrite, WriteReg10);
  and and_11 (and_11_out, RegWrite, WriteReg11);
  and and_12 (and_12_out, RegWrite, WriteReg12);
  and and_13 (and_13_out, RegWrite, WriteReg13);
  and and_14 (and_14_out, RegWrite, WriteReg14);
  and and_15 (and_15_out, RegWrite, WriteReg15);
  and and_16 (and_16_out, RegWrite, WriteReg16);
  Register #(.Bits(32)) Reg9 (.D(WriteData), .C(Clock), .en(and_9_out), .Q(Reg9Output));
  Register #(.Bits(32)) Reg10 (.D(WriteData), .C(Clock), .en(and_10_out), .Q(Reg10Output));
  Register #(.Bits(32)) Reg11 (.D(WriteData), .C(Clock), .en(and_11_out), .Q(Reg11Output));
  Register #(.Bits(32)) Reg12 (.D(WriteData), .C(Clock), .en(and_12_out), .Q(Reg12Output));
  Register #(.Bits(32)) Reg13 (.D(WriteData), .C(Clock), .en(and_13_out), .Q(Reg13Output));
  Register #(.Bits(32)) Reg14 (.D(WriteData), .C(Clock), .en(and_14_out), .Q(Reg14Output));
  Register #(.Bits(32)) Reg15 (.D(WriteData), .C(Clock), .en(and_15_out), .Q(Reg15Output));
  Register #(.Bits(32)) Reg16 (.D(WriteData), .C(Clock), .en(and_16_out), .Q(Reg16Output));
  Multiplexer #(.Selector_Bits(5), .Bits(32)) multiplexer_2 (
    .sel(ReadReg2), .in_0({32{1'b0}}), .in_1(Reg1Output), .in_2(Reg2Output), .in_3(Reg3Output),
    .in_4(Reg4Output), .in_5(Reg5Output), .in_6(Reg6Output), .in_7(Reg7Output), .in_8(Reg8Output),
    .in_9(Reg9Output), .in_10(Reg10Output), .in_11(Reg11Output), .in_12(Reg12Output), .in_13(Reg13Output),
    .in_14(Reg14Output), .in_15(Reg15Output), .in_16(Reg16Output), .in_17(Reg17Output), .in_18(Reg18Output),
    .in_19(Reg19Output), .in_20(Reg20Output), .in_21(Reg21Output), .in_22(Reg22Output), .in_23(Reg23Output),
    .in_24(Reg24Output), .in_25(Reg25Output), .in_26(Reg26Output), .in_27(Reg27Output), .in_28(Reg28Output),
    .in_29(Reg29Output), .in_30(Reg30Output), .in_31(Reg31Output), .out(ReadData2));
  and and_17 (and_17_out, RegWrite, WriteReg17);
  and and_18 (and_18_out, RegWrite, WriteReg18);
  and and_19 (and_19_out, RegWrite, WriteReg19);
  and and_20 (and_20_out, RegWrite, WriteReg20);
  and and_21 (and_21_out, RegWrite, WriteReg21);
  and and_22 (and_22_out, RegWrite, WriteReg22);
  and and_23 (and_23_out, RegWrite, WriteReg23);
  and and_24 (and_24_out, RegWrite, WriteReg24);
  Register #(.Bits(32)) Reg17 (.D(WriteData), .C(Clock), .en(and_17_out), .Q(Reg17Output));
  Register #(.Bits(32)) Reg18 (.D(WriteData), .C(Clock), .en(and_18_out), .Q(Reg18Output));
  Register #(.Bits(32)) Reg19 (.D(WriteData), .C(Clock), .en(and_19_out), .Q(Reg19Output));
  Register #(.Bits(32)) Reg20 (.D(WriteData), .C(Clock), .en(and_20_out), .Q(Reg20Output));
  Register #(.Bits(32)) Reg21 (.D(WriteData), .C(Clock), .en(and_21_out), .Q(Reg21Output));
  Register #(.Bits(32)) Reg22 (.D(WriteData), .C(Clock), .en(and_22_out), .Q(Reg22Output));
  Register #(.Bits(32)) Reg23 (.D(WriteData), .C(Clock), .en(and_23_out), .Q(Reg23Output));
  Register #(.Bits(32)) Reg24 (.D(WriteData), .C(Clock), .en(and_24_out), .Q(Reg24Output));
  and and_25 (and_25_out, RegWrite, WriteReg25);
  and and_26 (and_26_out, RegWrite, WriteReg26);
  and and_27 (and_27_out, RegWrite, WriteReg27);
  and and_28 (and_28_out, RegWrite, WriteReg28);
  and and_29 (and_29_out, RegWrite, WriteReg29);
  and and_30 (and_30_out, RegWrite, WriteReg30);
  and and_31 (and_31_out, RegWrite, WriteReg31);
  Register #(.Bits(32)) Reg25 (.D(WriteData), .C(Clock), .en(and_25_out), .Q(Reg25Output));
  Register #(.Bits(32)) Reg26 (.D(WriteData), .C(Clock), .en(and_26_out), .Q(Reg26Output));
  Register #(.Bits(32)) Reg27 (.D(WriteData), .C(Clock), .en(and_27_out), .Q(Reg27Output));
  Register #(.Bits(32)) Reg28 (.D(WriteData), .C(Clock), .en(and_28_out), .Q(Reg28Output));
  Register #(.Bits(32)) Reg29 (.D(WriteData), .C(Clock), .en(and_29_out), .Q(Reg29Output));
  Register #(.Bits(32)) Reg30 (.D(WriteData), .C(Clock), .en(and_30_out), .Q(Reg30Output));
  Register #(.Bits(32)) Reg31 (.D(WriteData), .C(Clock), .en(and_31_out), .Q(Reg31Output));

  // Other names for the same wires on the sheet: Clk = Clock
endmodule

/* Test case Register File Test:
WriteReg WriteData RegWrite Clock ReadReg1 ReadReg2 ReadData1 ReadData2

# $1 = 25
1 25 1 C 1 0 25 0

# $2 = 30
2 30 1 C 0 2 0 30

# $(N+1) = (N+1)
loop(N, 30)
	(N+1) (N+1) 1 C (N+1) (N) (N+1) (N)
end loop

# $(N+1) = N-60
loop(N, 30)
	(N+1) (N-60) 1 C (N+1) (N+1) (N-60) (N-60)
end loop

# Try writing to $0. This should not write anything
0 25 1 C 0 0 0 0

# try writing when RegWrite = 0
# (the registers should still have their old values)
loop(N, 30)
	(N+1) (N+80) 0 C (N+1) (N+1) (N-60) (N-60)
end loop
*/
